# Fritzing sketch ragse nor  (saved by Fritzing 0.9.4)
breadboards: 1

parts:
  LED1 = LED - 5mm [color="White (4500K)" package="5 mm [THT]"]  # not connected
  LED2 = LED - 5mm [color="Blue (525nm)" package="5 mm [THT]"]
  LED3 = LED - 5mm [color="Yellow (585nm)" package="5 mm [THT]"]
  LED4 = LED - 5mm [color="Red (633nm)" package="5 mm [THT]"]
  LED5 = LED - 5mm [color="Orange (612nm)" package="5 mm [THT]"]
  LED6 = LED - 5mm [color="Green (555nm)" package="5 mm [THT]"]
  LED7 = LED - 5mm [color="Infrared (880nm)" package="5 mm [THT]"]
  LED8 = LED - 5mm [color="Red (633nm)" package="5 mm [THT]"]
  R1 = Resistor [tolerance=±5% resistance=220 package=THT]
  R2 = Resistor [tolerance=±5% resistance=220 package=THT]
  R3 = Resistor [tolerance=±5% resistance=220 package=THT]
  R4 = Resistor [tolerance=±5% resistance=220 package=THT]
  R5 = Resistor [tolerance=±5% resistance=220 package=THT]
  R6 = Resistor [tolerance=±5% resistance=220 package=THT]
  R7 = Resistor [tolerance=±5% resistance=220 package=THT]
  R8 = Resistor [tolerance=±5% resistance=220 package=THT]
  S1 = Pushbutton [package="[THT]"]
  S2 = Pushbutton [package="[THT]"]
  S3 = Pushbutton [package="[THT]"]
  R9 = Resistor [tolerance=±5% resistance=220 package=THT]
  R10 = Resistor [tolerance=±5% resistance=220 package=THT]
  R11 = Resistor [tolerance=±5% resistance=220 package=THT]
  Part1 = Arduino Uno (Rev3)

nets:
  N1: LED2.cathode, Part1.D3_PWM
  N2: LED2.anode, R2.Pin_0
  N3: LED3.cathode, Part1.D4
  N4: LED3.anode, R3.Pin_0
  N5: LED4.cathode, Part1.D5_PWM
  N6: LED4.anode, R4.Pin_0
  N7: LED5.cathode, Part1.D6_PWM
  N8: LED5.anode, R5.Pin_0
  N9: LED6.cathode, Part1.D7
  N10: LED6.anode, R6.Pin_0
  N11: LED7.cathode, Part1.D8
  N12: LED7.anode, R7.Pin_0
  N13: LED8.cathode, Part1.D9_PWM
  N14: LED8.anode, R8.Pin_0
  N15: R1.Pin_1, R2.Pin_1, R3.Pin_1, R4.Pin_1, R5.Pin_1, R6.Pin_1, R7.Pin_1, R8.Pin_1, S1.Pin_3, S1.Pin_4, S2.Pin_3, S2.Pin_4, S3.Pin_3, S3.Pin_4, R9.Pin_0, R10.Pin_0, R11.Pin_0, Part1.GND
  N16: S1.Pin_1, S1.Pin_2, R9.Pin_1, Part1.A2
  N17: S2.Pin_1, S2.Pin_2, R10.Pin_1, Part1.A1
  N18: S3.Pin_1, S3.Pin_2, R11.Pin_1, Part1.A0
